# Fritzing sketch mozzi (saved by Fritzing 0.9.2b)

parts:
  Part1 = Arduino Uno (Rev3)
  U1 = MIDI_CONN_FEMALE_SUPPORT [package=din_5_female_support]  # not connected
  SP1 = SPEAKER [package=pcb_mount_speaker]

nets:
  N1: Part1.D9_PWM, SP1.-
  N2: Part1.GND, SP1.+
